# Fritzing sketch aws-temperature-sensor (saved by Fritzing 0.9.3b)
breadboards: 1

parts:
  U1 = Onion Omega2 and Expansion Dock
  R1 = Resistor [tolerance=±5% resistance=4.7k package="0603 [SMD]"]
  DS2 = DS18B20 1-Wire Temperature Sensor Probe Cable

nets:
  GND: U1.GND, DS2.GND
  3.3V: U1.3.3V, R1.Pin_1, DS2.VDD
  N1: U1.GPIO18, R1.Pin_0, DS2.shield

custom parts:
  Onion Omega2 and Expansion Dock: Onion Omega2 IoT Computer on Expansion Dock Omega2: - 580 Mhz MIPS CPU - 64MB RAM, Omega2+: 128MB RAM - 16MB Flash, Omega2+: 32M Flash - LEDE Linux OS - USB2.0 - 2.4GHz b/g/n WiFi - 15GPIO - 2PWM - 2 UART - 1 I2C - 1 SPI - 1 I2S - Micro-SD Card Slot (Omega2+ only) Expansion Dock: - Micro USB Port: Power and USB-to-Serial - USB Type-A Host Port - Reset Button - Power Switch - RGB LED -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
